# Fritzing sketch functions (saved by Fritzing 1.0.6)
breadboards: 1

parts:
  Part1 = node32s
  R1 = Resistor [tolerance=±5% resistance=220 package="0402 [SMD]"]
  LED1 = smd LED [color="Red (633nm)" package="0603 [SMD]"]
  LED2 = smd LED [color="Yellow (585nm)" package="0603 [SMD]"]
  R2 = Resistor [tolerance=±5% resistance=220 package="0402 [SMD]"]
  R3 = Resistor [tolerance=±5% resistance=220 package="0402 [SMD]"]
  LED3 = smd LED [color="Green (555nm)" package="0603 [SMD]"]

nets:
  N1: Part1.IO32, LED1.anode
  N2: Part1.IO33, LED2.anode
  N3: Part1.IO25, LED3.anode
  N4: Part1.V_BATT, R1.Pin_0, R2.Pin_0, R3.Pin_0
  N5: R1.Pin_1, LED1.cathode
  N6: LED2.cathode, R2.Pin_1
  N7: R3.Pin_1, LED3.cathode

notes:
  220Ω Resistor
  Short Leg LED (–) Cathode
